# Fritzing sketch BreadboardLayout (saved by Fritzing 0.9.2b)
breadboards: 1

parts:
  Part1 = Arduino Uno (Rev3)
  D1 = LED_BARGRAPH_10 [package=led_bargaph_10]
  U1 = POT [package=pot_mammoth]
  S1 = Momentary Switch [package=ksa_sealed_tac_switch]
  R1 = Resistor [tolerance=±5% resistance=10k package=THT]

nets:
  N1: Part1.A3, U1.A
  N2: Part1.A4/SDA, D1.SDA
  N3: Part1.A5/SCL, D1.SCL
  N4: Part1.D2, S1.4
  N5: Part1.ioref, D1.VCC, U1.E, S1.2
  GND: Part1.GND, D1.Gnd, U1.S, R1.Pin_0
  N6: S1.3, R1.Pin_1

custom parts:
  LED_BARGRAPH_10: 10-Segment LED Bar Graph SFE part numbers: COM-09935 (red, Vf = 2.1V, Ifmax = 20mA) COM-09936 (yellow, Vf = 2.1V, Ifmax = 20mA) COM-09937 (blue, Vf = 3.4V, Ifmax = 20mA) COM-09938 (green, Vf = 3.4V, Ifmax = 20mA)
